// Logisim project cpuproject.circ as structural Verilog
module ULA (
  input  [15:0] A,
  input  [15:0] B,
  input  [3:0] OP,
  output [15:0] R,
  output R1
);
endmodule

module XOR (
  input  in_1,
  input  in_2,
  output out_3
);

  wire and_1_out, and_2_out, not_1_out, not_2_out;

  not not_1 (not_1_out, in_1);
  not not_2 (not_2_out, in_2);
  and and_1 (and_1_out, not_1_out, in_2);
  and and_2 (and_2_out, in_1, not_2_out);
  or or_1 (out_3, and_1_out, and_2_out);
endmodule

module SOMA1 (
  input  in_1,
  input  in_2,
  output out_3,
  output out_4
);

  and and_1 (out_3, in_1, in_2);
  XOR xor_1 (.in_1(in_1), .in_2(in_2), .out_3(out_4));
endmodule

module SOMA3 (
  input  [2:0] in_1,
  input  [2:0] in_2,
  output [2:0] out_3,
  output out_4
);
endmodule
